// Digital circuit Ring4Bits.dig as structural Verilog
module Ring4Bits (
  input  CLK,
  input  Stop,
  output D0,
  output D1,
  output D2,
  output D3
);

  wire d_ff_1_nq, d_ff_2_nq, d_ff_3_nq, d_ff_4_nq, d_ff_5_nq, d_ff_6_nq, d_ff_7_nq, d_ff_8_nq, d_ff_9_nq,
       d_ff_10_nq, d_ff_11_nq, d_ff_12_nq, d_ff_13_nq, d_ff_14_nq, d_ff_15_nq, d_ff_16_nq, d_ff_17_nq,
       d_ff_18_nq, d_ff_19_nq, d_ff_20_nq, d_ff_21_nq, d_ff_22_nq, d_ff_23_nq, d_ff_27_nq, or_1_out;

  or or_1 (or_1_out, CLK, Stop);
  D_FF d_ff_1 (.D(d_ff_1_nq), .C(or_1_out), .nQ(d_ff_1_nq));  // open: Q
  D_FF d_ff_2 (.D(d_ff_2_nq), .C(d_ff_21_nq), .nQ(d_ff_2_nq));  // open: Q
  D_FF d_ff_3 (.D(d_ff_3_nq), .C(d_ff_22_nq), .nQ(d_ff_3_nq));  // open: Q
  D_FF d_ff_4 (.D(d_ff_4_nq), .C(d_ff_23_nq), .nQ(d_ff_4_nq));  // open: Q
  D_FF d_ff_5 (.D(d_ff_5_nq), .C(d_ff_1_nq), .nQ(d_ff_5_nq));  // open: Q
  D_FF d_ff_6 (.D(d_ff_6_nq), .C(d_ff_2_nq), .nQ(d_ff_6_nq));  // open: Q
  D_FF d_ff_7 (.D(d_ff_7_nq), .C(d_ff_3_nq), .nQ(d_ff_7_nq));  // open: Q
  D_FF d_ff_8 (.D(d_ff_8_nq), .C(d_ff_4_nq), .nQ(d_ff_8_nq));  // open: Q
  D_FF d_ff_9 (.D(d_ff_9_nq), .C(d_ff_5_nq), .nQ(d_ff_9_nq));  // open: Q
  D_FF d_ff_10 (.D(d_ff_10_nq), .C(d_ff_6_nq), .nQ(d_ff_10_nq));  // open: Q
  D_FF d_ff_11 (.D(d_ff_11_nq), .C(d_ff_7_nq), .nQ(d_ff_11_nq));  // open: Q
  D_FF d_ff_12 (.D(d_ff_12_nq), .C(d_ff_8_nq), .nQ(d_ff_12_nq));  // open: Q
  D_FF d_ff_13 (.D(d_ff_13_nq), .C(d_ff_9_nq), .nQ(d_ff_13_nq));  // open: Q
  D_FF d_ff_14 (.D(d_ff_14_nq), .C(d_ff_10_nq), .nQ(d_ff_14_nq));  // open: Q
  D_FF d_ff_15 (.D(d_ff_15_nq), .C(d_ff_11_nq), .nQ(d_ff_15_nq));  // open: Q
  D_FF d_ff_16 (.D(d_ff_16_nq), .C(d_ff_12_nq), .nQ(d_ff_16_nq));  // open: Q
  D_FF d_ff_17 (.D(d_ff_17_nq), .C(d_ff_13_nq), .nQ(d_ff_17_nq));  // open: Q
  D_FF d_ff_18 (.D(d_ff_18_nq), .C(d_ff_14_nq), .nQ(d_ff_18_nq));  // open: Q
  D_FF d_ff_19 (.D(d_ff_19_nq), .C(d_ff_15_nq), .nQ(d_ff_19_nq));  // open: Q
  D_FF d_ff_20 (.D(d_ff_20_nq), .C(d_ff_16_nq), .nQ(d_ff_20_nq));  // open: Q
  D_FF d_ff_21 (.D(d_ff_21_nq), .C(d_ff_17_nq), .nQ(d_ff_21_nq));  // open: Q
  D_FF d_ff_22 (.D(d_ff_22_nq), .C(d_ff_18_nq), .nQ(d_ff_22_nq));  // open: Q
  D_FF d_ff_23 (.D(d_ff_23_nq), .C(d_ff_19_nq), .nQ(d_ff_23_nq));  // open: Q
  D_FF d_ff_24 (.D(d_ff_27_nq), .C(d_ff_20_nq), .Q(D0));  // open: nQ
  D_FF d_ff_25 (.D(D0), .C(d_ff_20_nq), .Q(D1));  // open: nQ
  D_FF d_ff_26 (.D(D1), .C(d_ff_20_nq), .Q(D2));  // open: nQ
  D_FF d_ff_27 (.D(D2), .C(d_ff_20_nq), .Q(D3), .nQ(d_ff_27_nq));
endmodule
